// Logisim project 8bit_CPU.circ as structural Verilog: 2 circuits, main circuit main
module main (
  input  [7:0] DataWriter,
  input  WriteToBus,
  input  in_3
);

  wire AI, ALUO, AO, BI, BO, CE, CL, clock_1_out, CO, HLT, II, IO, JUMP, MI, not_1_out, not_2_out, RI, RO, SU;
  wire [7:0] AdressRegister_q, alu_1_out_4, controlled_buffer_1_out, InstructionCounter_q,
       InstructionRegister_q, PC_q, ram_1_dout, RegisterA_q, RegisterB_q;
  wire [7:7] IR_ROM1_data;

  Clock clock_1 (.out(clock_1_out));
  not not_1 (not_1_out, HLT);
  and and_1 (CL, clock_1_out, not_1_out);
  RAM ram_1 (.addr(AdressRegister_q), .we(RI), .oe(1'b1), .clk(CL), .din(controlled_buffer_1_out), .dout(ram_1_dout));
  Register AdressRegister (.D(controlled_buffer_1_out), .en(MI), .clk(CL), .Q(AdressRegister_q));  // open: clr
  Counter PC (
    .clr(in_3), .load(JUMP), .up(1'b1), .count(CE), .clk(CL), .D(controlled_buffer_1_out), .Q(PC_q));  // open: carry
  Register RegisterA (.D(controlled_buffer_1_out), .en(AI), .clk(CL), .Q(RegisterA_q));  // open: clr
  Register RegisterB (.D(controlled_buffer_1_out), .en(BI), .clk(CL), .Q(RegisterB_q));  // open: clr
  assign controlled_buffer_1_out = AO ? RegisterA_q : 8'bz;  // Controlled_Buffer controlled_buffer_1
  assign controlled_buffer_1_out = ALUO ? alu_1_out_4 : 8'bz;  // Controlled_Buffer controlled_buffer_2
  ALU alu_1 (.RegA(RegisterA_q), .RegB(RegisterB_q), .Su(SU), .out_4(alu_1_out_4));
  assign controlled_buffer_1_out = BO ? RegisterB_q : 8'bz;  // Controlled_Buffer controlled_buffer_3
  assign controlled_buffer_1_out = RO ? ram_1_dout : 8'bz;  // Controlled_Buffer controlled_buffer_4
  // Probe on controlled_buffer_1_out
  assign controlled_buffer_1_out = CO ? PC_q : 8'bz;  // Controlled_Buffer controlled_buffer_5
  assign controlled_buffer_1_out = WriteToBus ? DataWriter : 8'bz;  // Controlled_Buffer controlled_buffer_6
  not not_2 (not_2_out, CL);
  Register InstructionRegister (
    .D(controlled_buffer_1_out), .en(II), .clk(CL), .Q(InstructionRegister_q));  // open: clr
  Counter InstructionCounter (
    .up(1'b1), .count(1'b1), .clk(not_2_out), .Q(InstructionCounter_q));  // open: clr, load, D, carry
  assign controlled_buffer_1_out = IO ? InstructionRegister_q : 8'bz;  // Controlled_Buffer controlled_buffer_7
  ROM #(.addrWidth(16), .dataWidth(16)) IR_ROM1 (
    .addr({InstructionRegister_q, InstructionCounter_q}),
    .data({HLT, MI, RI, RO, IO, II, AI, AO, IR_ROM1_data[7], ALUO, SU, BI, BO, CE, CO, JUMP}));

  // Notes on the sheet:
  //   contents of IR_ROM1 (hex, n*v repeats v):
  //   4002 1404
endmodule

module ALU (
  input  [7:0] RegA,
  input  [7:0] RegB,
  input  Su,
  output [7:0] out_4
);

  wire adder_1_cout;
  wire [7:0] bit_extender_1_out, xor_1_out;

  assign bit_extender_1_out = {{7{Su}}, Su};  // Bit_Extender bit_extender_1
  assign xor_1_out = RegB ^ bit_extender_1_out;  // XOR_Gate xor_1, 8 bits wide
  Adder adder_1 (.a(RegA), .b(xor_1_out), .out(out_4), .cin(Su), .cout(adder_1_cout));
endmodule
